# Fritzing sketch Carrero (saved by Fritzing 0.9.3b)
circuit board: 8.60233cm x 5.70474cm

parts:
  M1 = DC Motor
  M2 = DC Motor
  U1 = L298 [package=multiwatt15]
  VCC1 = Battery block 9V
  Raspberry_Pi1 = Raspberry Pi 2

nets (from the schematic view):
  N1: M1.pin_1, U1.OUT1
  N2: M1.pin_2, U1.OUT2
  N3: M2.pin_1, U1.OUT3
  N4: M2.pin_2, U1.OUT4
  N5: U1.VS, U1.ENA, U1.ENB, VCC1.+
  N6: U1.IN1, Raspberry_Pi1.GPIO17
  N7: U1.IN2, Raspberry_Pi1.GPIO22
  GND: U1.GND, VCC1.-, Raspberry_Pi1.GND
  N8: U1.IN3, Raspberry_Pi1.GPIO23
  N9: U1.IN4, Raspberry_Pi1.GPIO24

// code stored in the sketch: Carrero_code.ino
// connect motor controller pins to Arduino digital pins
// motor one
int enA = 10;
int in1 = 9;
int in2 = 8;
// motor two
int enB = 5;
int in3 = 7;
int in4 = 6;
void setup()
{
  // set all the motor control pins to outputs
  pinMode(enA, OUTPUT);
  pinMode(enB, OUTPUT);
  pinMode(in1, OUTPUT);
  pinMode(in2, OUTPUT);
  pinMode(in3, OUTPUT);
  pinMode(in4, OUTPUT);
}
void demoOne()
{
  // this function will run the motors in both directions at a fixed speed
  // turn on motor A
  digitalWrite(in1, HIGH);
  digitalWrite(in2, LOW);
  // set speed to 200 out of possible range 0~255
  analogWrite(enA, 200);
  // turn on motor B
  digitalWrite(in3, HIGH);
  digitalWrite(in4, LOW);
  // set speed to 200 out of possible range 0~255
  analogWrite(enB, 200);
  delay(2000);
  // now change motor directions
  digitalWrite(in1, LOW);
  digitalWrite(in2, HIGH);  
  digitalWrite(in3, LOW);
  digitalWrite(in4, HIGH); 
  delay(2000);
  // now turn off motors
  digitalWrite(in1, LOW);
  digitalWrite(in2, LOW);  
  digitalWrite(in3, LOW);
  digitalWrite(in4, LOW);
}
void demoTwo()
{
  // this function will run the motors across the range of possible speeds
  // note that maximum speed is determined by the motor itself and the operating voltage
  // the PWM values sent by analogWrite() are fractions of the maximum speed possible 
  // by your hardware
  // turn on motors
  digitalWrite(in1, LOW);
  digitalWrite(in2, HIGH);  
  digitalWrite(in3, LOW);
  digitalWrite(in4, HIGH); 
  // accelerate from zero to maximum speed
  for (int i = 0; i < 256; i++)
  {
    analogWrite(enA, i);
    analogWrite(enB, i);
    delay(20);
  } 
  // decelerate from maximum speed to zero
  for (int i = 255; i >= 0; --i)
  {
    analogWrite(enA, i);
    analogWrite(enB, i);
    delay(20);
  } 
  // now turn off motors
  digitalWrite(in1, LOW);
  digitalWrite(in2, LOW);  
  digitalWrite(in3, LOW);
  digitalWrite(in4, LOW);  
}
void loop()
{
  demoOne();
  delay(1000);
  demoTwo();
  delay(1000);
}

// code stored in the sketch: motor.py.ino
import time
import RPi.GPIO as GPIO

mode=GPIO.getmode()

GPIO.cleanup()

pins = {
	"motorL_Positive": 22,
	"motorL_Negative": 20,
	"motorR_Positive": 19,
	"motorR_Negative": 21,
}

sleeptime=1

GPIO.setmode(GPIO.BOARD)

for key in pins.keys():
	GPIO.setup(pins[key], GPIO.OUT)

def forward(x):
	GPIO.output(Forward, GPIO.HIGH)
	print("Moving Forward")
	time.sleep(x)
	GPIO.output(Forward, GPIO.LOW)

def reverse(x):
	GPIO.output(Backward, GPIO.HIGH)
	print("Moving Backward")
	time.sleep(x)
	GPIO.output(Backward, GPIO.LOW)

while (1):

	forward(5)

	reverse(5)
	GPIO.cleanup()
